# Fritzing sketch HeatPump (saved by Fritzing 0.9.3b)
perfboards: 1

parts:
  6A = RELAY [package=OJ]
  U2 = Sharp PC817 [package=THT]
  Q1 = NPN-Transistor [package="TO92 [THT]"]
  D1 = Diode [package=diode-1n4001]
  R1 = Resistor [tolerance=±5% resistance=1k package=THT]
  5V_1A = DC Power [voltage=5]
  220V_AC = AC Power [voltage=5 frequency=60]
  12V_1A = DC Power [voltage=5]
  R2 = Resistor [tolerance=±5% resistance=220 package=THT]
  Arduino_Mega_2560 = Arduino Mega 2560 (Rev3)
  SD_Card_Breakout = Adafruit MicroSD card breakout board [part_number="Adafruit #254"]
  Optional_RTC = Adafruit DS1307 RTC Breakout [part_number="Adafruit #264"]
  Outside_Temperature = DS18B20 1-Wire Temperature Sensor [part_number=DS18B20]
  Ice_Buildup_sensor = Infrared Proximity Sensor
  R3 = Resistor [tolerance=±5% resistance=3.3 package=THT]
  Temperature_probe_Water_In = Resistor [tolerance=±0.25% resistance=22k package=THT]
  R4 = Resistor [tolerance=±5% resistance=4.7k package=THT]

nets:
  N1: 6A.COIL2, Q1.C, D1.A
  Water Pump Relays: 6A.MAIN
  N2: 6A.NO, 220V_AC.V+
  N3: 6A.COIL1, U2.Pin_4, D1.C, 5V_1A.V+
  N4: U2.Pin_1, R2.Pin_0
  GND: U2.Pin_2, 12V_1A.V-, Arduino_Mega_2560.GND, SD_Card_Breakout.GND, Optional_RTC.GND, Outside_Temperature.GND, Ice_Buildup_sensor.GND, Temperature_probe_Water_In.Pin_1
  N5: U2.Pin_3, R1.Pin_1
  N6: Q1.E, 5V_1A.V-
  N7: Q1.B, R1.Pin_0
  N8: 12V_1A.V+, Arduino_Mega_2560.VIN
  N9: R2.Pin_1, Arduino_Mega_2560.D2_PWM
  Temp. Outside: Arduino_Mega_2560.A8
  Temp. Evaporator: Arduino_Mega_2560.A9
  Temp. Water Out: Arduino_Mega_2560.A10
  N10: Arduino_Mega_2560.A11, R3.Pin_1, Temperature_probe_Water_In.Pin_0
  Ice buildup sensor: Arduino_Mega_2560.A6
  Temp. Hot Water: Arduino_Mega_2560.A7
  N11: Arduino_Mega_2560.SCL, Optional_RTC.SCL
  N12: Arduino_Mega_2560.SDA, Optional_RTC.SDA
  VCC: Arduino_Mega_2560.5V, SD_Card_Breakout.VCC, Optional_RTC.VCC, Outside_Temperature.VDD, Ice_Buildup_sensor.Vcc, R3.Pin_0, R4.Pin_0
  Heater relay: Arduino_Mega_2560.D4_PWM
  Fan relay: Arduino_Mega_2560.D5_PWM
  TXV valve relay: Arduino_Mega_2560.D6_PWM
  Compressor relay: Arduino_Mega_2560.D7_PWM
  N13: Arduino_Mega_2560.D22, Outside_Temperature.DQ, R4.Pin_1
  N14: Arduino_Mega_2560.D50, SD_Card_Breakout.DO
  N15: Arduino_Mega_2560.D51, SD_Card_Breakout.DI
  N16: Arduino_Mega_2560.D52, SD_Card_Breakout.CLK
  N17: Arduino_Mega_2560.D53, SD_Card_Breakout.CS
  A6: Ice_Buildup_sensor.Vout

notes:
  Relay scheme
  duplicated for other relays
  Ice buildup + Temperature sensor PCB

custom parts:
  Adafruit MicroSD card breakout board: Not just a simple breakout board, this microSD adapter goes the extra mile - designed for ease of use. Onboard 5v->3v regulator provides 150mA for power-hungry cards 3v level shifting means you can use this with ease on either 3v or 5v systems Uses a proper level shifting chip, not resistors: less problems, and faster read/write access Use 3 or 4 digital pins to read and write 2Gb+ of storage!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
  Adafruit DS1307 RTC Breakout: This is a great battery-backed real time clock (RTC) that allows your microcontroller project to keep track of time even if it is reprogrammed, or if the power is lost. Perfect for datalogging, clock-building, time stamping, timers and alarms, etc. The DS1307 is the most popular RTC - but it requires 5V power to work (although we've used it with 5V power and 3.3V logic successfully) PCB &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
